// Logisim project S1-T19-Simplified.circ as structural Verilog: 4 circuits, main circuit main
module main (
  input  KEY,
  input  in_2,
  input  NONCE,
  input  input_1,
  input  input_0,
  output out_6
);

  wire and_1_out, and_2_out, and_4_out, and_5_out, d_ff_1_q, d_ff_1_qn, d_ff_2_q, d_ff_2_qn, decoder_1_out_3,
       decoder_1_out_4, decoder_1_out_5, decoder_1_out_6, or_1_out, plain_text_input_1_bit_value,
       plain_text_input_1_flag, quarter_round_generator_1_a_2, quarter_round_generator_1_b_2,
       quarter_round_generator_1_c_2, quarter_round_generator_1_d_2, xor_1_out;

  Plain_Text_Input plain_text_input_1 (
    .input_1(input_1), .input_0(input_0), .flag(plain_text_input_1_flag),
    .Bit_Value(plain_text_input_1_bit_value));
  D_Flip_Flop d_ff_1 (
    .clk(plain_text_input_1_flag), .D(d_ff_1_qn), .Q(d_ff_1_q), .Qn(d_ff_1_qn));  // open: preset, en, reset
  D_Flip_Flop d_ff_2 (.clk(d_ff_1_qn), .D(d_ff_2_qn), .Q(d_ff_2_q), .Qn(d_ff_2_qn));  // open: preset, en, reset
  Decoder decoder_1 (
    .MSB(d_ff_2_q), .LSB(d_ff_1_q), .out_3(decoder_1_out_3), .out_4(decoder_1_out_4),
    .out_5(decoder_1_out_5), .out_6(decoder_1_out_6));
  and and_1 (and_1_out, decoder_1_out_3, quarter_round_generator_1_a_2);
  Quarter_Round_Generator quarter_round_generator_1 (
    .A(d_ff_1_q), .B(KEY), .C(in_2), .D(NONCE), .a_2(quarter_round_generator_1_a_2),
    .b_2(quarter_round_generator_1_b_2), .c_2(quarter_round_generator_1_c_2),
    .d_2(quarter_round_generator_1_d_2));
  and and_2 (and_2_out, decoder_1_out_4, quarter_round_generator_1_b_2);
  or or_1 (or_1_out, and_1_out, and_2_out, and_4_out, and_5_out);
  xor xor_1 (xor_1_out, plain_text_input_1_bit_value, or_1_out);
  and and_3 (out_6, plain_text_input_1_flag, xor_1_out);
  and and_4 (and_4_out, decoder_1_out_5, quarter_round_generator_1_c_2);
  and and_5 (and_5_out, decoder_1_out_6, quarter_round_generator_1_d_2);

  // Notes on the sheet:
  //   MAIN CIRCUIT
  //   Logisim Implementation for ChaCha20 Stream Cipher
endmodule

// QRG
module Quarter_Round_Generator (
  input  A,
  input  B,
  input  C,
  input  D,
  output a_2,
  output b_2,
  output c_2,
  output d_2
);

  wire adder_1_out, adder_3_out, Xor1_out, Xor2_out;

  Adder #(.width(1)) adder_1 (.a(B), .b(A), .out(adder_1_out));  // open: cin, cout
  xor Xor2 (Xor2_out, B, adder_3_out);
  xor Xor4 (b_2, Xor2_out, c_2);
  Adder #(.width(1)) adder_2 (.a(Xor2_out), .b(adder_1_out), .out(a_2));  // open: cin, cout
  xor Xor1 (Xor1_out, adder_1_out, D);
  xor Xor3 (d_2, a_2, Xor1_out);
  Adder #(.width(1)) adder_3 (.a(Xor1_out), .b(C), .out(adder_3_out));  // open: cin, cout
  Adder #(.width(1)) adder_4 (.a(adder_3_out), .b(d_2), .out(c_2));  // open: cin, cout

  // Notes on the sheet:
  //   Add1
  //   Add3
  //   QUARTER ROUND GENERATOR
  //   Add2
  //   Add4
endmodule

// PTI
module Plain_Text_Input (
  input  input_1,
  input  input_0,
  output flag,
  output Bit_Value
);

  xor xor_1 (flag, input_1, input_0);

  assign Bit_Value = input_1;

  // Notes on the sheet:
  //   PLAIN TEXT INPUT
endmodule

// DECODER
module Decoder (
  input  MSB,
  input  LSB,
  output out_3,
  output out_4,
  output out_5,
  output out_6
);

  wire not_1_out, not_2_out;

  not not_1 (not_1_out, MSB);
  not not_2 (not_2_out, LSB);
  and and_1 (out_3, not_1_out, not_2_out);
  and and_2 (out_4, not_1_out, LSB);
  and and_3 (out_5, MSB, not_2_out);
  and and_4 (out_6, MSB, LSB);

  // Notes on the sheet:
  //   DECODER
endmodule
