// Logisim project S1-T19.circ as structural Verilog: 7 circuits, main circuit main
module main (
  input  LOCK,
  input  COUNTER_INITIAL,
  input  in_3,
  input  in_4,
  input  in_5,
  input  _8_BIT_KEY,
  input  in_7,
  input  in_8,
  input  in_9,
  input  in_10,
  input  in_11,
  input  NONCE,
  input  in_13,
  input  INPUT_1,
  input  INPUT_0,
  output OUTPUT_CIPHERTEXT
);

  wire bit_selector_1_out_19, key_stream_generator_1_out_17, key_stream_generator_1_out_18,
       key_stream_generator_1_out_19, key_stream_generator_1_out_20, key_stream_generator_1_out_21,
       key_stream_generator_1_out_22, key_stream_generator_1_out_23, key_stream_generator_1_out_24,
       key_stream_generator_1_out_25, key_stream_generator_1_out_26, key_stream_generator_1_out_27,
       key_stream_generator_1_out_28, key_stream_generator_1_out_29, key_stream_generator_1_out_30,
       key_stream_generator_1_out_31, key_stream_generator_1_out_32, n2_bit_counter_1_lsb,
       n2_bit_counter_1_msb, not_1_out, plain_text_input_1_bit_value, plain_text_input_1_flag, xor_1_out;

  Plain_Text_Input plain_text_input_1 (
    .input_1(INPUT_1), .input_0(INPUT_0), .flag(plain_text_input_1_flag),
    .Bit_Value(plain_text_input_1_bit_value));
  _2_Bit_Counter u_2_bit_counter_1 (
    .in_1(plain_text_input_1_flag), .INIT_LSB(in_3), .INIT_MSB(COUNTER_INITIAL), .Lock(LOCK),
    .LSB(n2_bit_counter_1_lsb), .MSB(n2_bit_counter_1_msb));
  not not_1 (not_1_out, 1'b1);
  Key_Stream_Generator key_stream_generator_1 (
    .x(1'b1), .x_2(1'b1), .x_3(not_1_out), .x_4(1'b1), .in_5(in_4), .in_6(in_5), .Key(_8_BIT_KEY),
    .in_8(in_7), .in_9(in_8), .in_10(in_9), .in_11(in_10), .in_12(in_11), .MSB(n2_bit_counter_1_msb),
    .LSB(n2_bit_counter_1_lsb), .Nonce(NONCE), .in_16(in_13), .out_17(key_stream_generator_1_out_17),
    .out_18(key_stream_generator_1_out_18), .out_19(key_stream_generator_1_out_19),
    .out_20(key_stream_generator_1_out_20), .out_21(key_stream_generator_1_out_21),
    .out_22(key_stream_generator_1_out_22), .out_23(key_stream_generator_1_out_23),
    .out_24(key_stream_generator_1_out_24), .out_25(key_stream_generator_1_out_25),
    .out_26(key_stream_generator_1_out_26), .out_27(key_stream_generator_1_out_27),
    .out_28(key_stream_generator_1_out_28), .out_29(key_stream_generator_1_out_29),
    .out_30(key_stream_generator_1_out_30), .out_31(key_stream_generator_1_out_31),
    .out_32(key_stream_generator_1_out_32));
  Bit_Selector bit_selector_1 (
    .FLAG(plain_text_input_1_flag), .LOCK(LOCK), .BIT_SELECTOR(key_stream_generator_1_out_22),
    .in_2(key_stream_generator_1_out_17), .in_3(key_stream_generator_1_out_18),
    .in_4(key_stream_generator_1_out_21), .in_5(key_stream_generator_1_out_19),
    .in_6(key_stream_generator_1_out_20), .in_7(key_stream_generator_1_out_23),
    .in_8(key_stream_generator_1_out_25), .in_9(key_stream_generator_1_out_26),
    .in_10(key_stream_generator_1_out_31), .in_11(key_stream_generator_1_out_27),
    .in_12(key_stream_generator_1_out_28), .in_13(key_stream_generator_1_out_29),
    .in_14(key_stream_generator_1_out_24), .in_15(key_stream_generator_1_out_30),
    .in_16(key_stream_generator_1_out_32), .out_19(bit_selector_1_out_19));
  xor xor_1 (xor_1_out, plain_text_input_1_bit_value, bit_selector_1_out_19);
  and and_1 (OUTPUT_CIPHERTEXT, plain_text_input_1_flag, xor_1_out);
  DotMatrix #(.matrixcols(1), .matrixrows(1)) dotmatrix_1 (.col0(key_stream_generator_1_out_17));
  DotMatrix #(.matrixcols(1), .matrixrows(1)) dotmatrix_2 (.col0(key_stream_generator_1_out_21));
  DotMatrix #(.matrixcols(1), .matrixrows(1)) dotmatrix_3 (.col0(key_stream_generator_1_out_30));
  DotMatrix #(.matrixcols(1), .matrixrows(1)) dotmatrix_4 (.col0(key_stream_generator_1_out_18));
  DotMatrix #(.matrixcols(1), .matrixrows(1)) dotmatrix_5 (.col0(key_stream_generator_1_out_27));
  DotMatrix #(.matrixcols(1), .matrixrows(1)) dotmatrix_6 (.col0(key_stream_generator_1_out_31));
  DotMatrix #(.matrixcols(1), .matrixrows(1)) dotmatrix_7 (.col0(key_stream_generator_1_out_28));
  DotMatrix #(.matrixcols(1), .matrixrows(1)) dotmatrix_8 (.col0(key_stream_generator_1_out_24));
  DotMatrix #(.matrixcols(1), .matrixrows(1)) dotmatrix_9 (.col0(key_stream_generator_1_out_25));
  DotMatrix #(.matrixcols(1), .matrixrows(1)) dotmatrix_10 (.col0(key_stream_generator_1_out_22));
  DotMatrix #(.matrixcols(1), .matrixrows(1)) dotmatrix_11 (.col0(key_stream_generator_1_out_19));
  DotMatrix #(.matrixcols(1), .matrixrows(1)) dotmatrix_12 (.col0(key_stream_generator_1_out_32));
  DotMatrix #(.matrixcols(1), .matrixrows(1)) dotmatrix_13 (.col0(key_stream_generator_1_out_29));
  DotMatrix #(.matrixcols(1), .matrixrows(1)) dotmatrix_14 (.col0(key_stream_generator_1_out_26));
  DotMatrix #(.matrixcols(1), .matrixrows(1)) dotmatrix_15 (.col0(key_stream_generator_1_out_23));
  DotMatrix #(.matrixcols(1), .matrixrows(1)) dotmatrix_16 (.col0(key_stream_generator_1_out_20));

  // Notes on the sheet:
  //   FLAG
  //   BIT VALUE
  //   MAIN CIRCUIT
  //   Logisim Implementation for ChaCha20 Stream Cipher
  //   User Instructions :
  //   => Set initial counter value, 8-bit key, nonce
  //   Matrix Obtained after 2 rounds of encryption
  //   => To reset the circuit, simply toggle the lock to 1 and then immediately to 0.
  //   => To input the plain text, use the switches provided for 0 and 1.
  //   => The counter has to be set with the lock turned to 1. Once the counter value is set, turn lock to 0.
  //   =>The output for a given bit has to be recorded using the output ciphertext bit when the input bit is on.
  //   Note* : If any bit is not recorded and is missed by the user, the circuit needs to be reset and the input has to be passed again to obtain from the beginning
endmodule

// KSG
module Key_Stream_Generator (
  input  x,
  input  x_2,
  input  x_3,
  input  x_4,
  input  in_5,
  input  in_6,
  input  Key,
  input  in_8,
  input  in_9,
  input  in_10,
  input  in_11,
  input  in_12,
  input  MSB,
  input  LSB,
  input  Nonce,
  input  in_16,
  output out_17,
  output out_18,
  output out_19,
  output out_20,
  output out_21,
  output out_22,
  output out_23,
  output out_24,
  output out_25,
  output out_26,
  output out_27,
  output out_28,
  output out_29,
  output out_30,
  output out_31,
  output out_32
);

  wire col_1_a_2, col_1_b_2, col_1_c_2, col_1_d_2, col_2_a_2, col_2_b_2, col_2_c_2, col_2_d_2, col_3_a_2,
       col_3_b_2, col_3_c_2, col_3_d_2, col_4_a_2, col_4_b_2, col_4_c_2, col_4_d_2;

  Quarter_Round_Generator col_1 (
    .A(x), .B(in_5), .C(in_6), .D(MSB), .a_2(col_1_a_2), .b_2(col_1_b_2), .c_2(col_1_c_2), .d_2(col_1_d_2));
  Quarter_Round_Generator quarter_round_generator_1 (
    .A(col_1_a_2), .B(col_2_b_2), .C(col_3_c_2), .D(col_4_d_2), .a_2(out_17), .b_2(out_18), .c_2(out_19),
    .d_2(out_20));
  Quarter_Round_Generator col_2 (
    .A(x_2), .B(Key), .C(in_8), .D(LSB), .a_2(col_2_a_2), .b_2(col_2_b_2), .c_2(col_2_c_2), .d_2(col_2_d_2));
  Quarter_Round_Generator quarter_round_generator_2 (
    .A(col_1_b_2), .B(col_2_c_2), .C(col_3_d_2), .D(col_4_a_2), .a_2(out_21), .b_2(out_22), .c_2(out_23),
    .d_2(out_24));
  Quarter_Round_Generator col_3 (
    .A(x_3), .B(in_9), .C(in_10), .D(Nonce), .a_2(col_3_a_2), .b_2(col_3_b_2), .c_2(col_3_c_2),
    .d_2(col_3_d_2));
  Quarter_Round_Generator quarter_round_generator_3 (
    .A(col_1_c_2), .B(col_2_d_2), .C(col_3_a_2), .D(col_4_b_2), .a_2(out_25), .b_2(out_26), .c_2(out_27),
    .d_2(out_28));
  Quarter_Round_Generator col_4 (
    .A(x_4), .B(in_11), .C(in_12), .D(in_16), .a_2(col_4_a_2), .b_2(col_4_b_2), .c_2(col_4_c_2),
    .d_2(col_4_d_2));
  Quarter_Round_Generator quarter_round_generator_4 (
    .A(col_1_d_2), .B(col_2_a_2), .C(col_3_b_2), .D(col_4_c_2), .a_2(out_29), .b_2(out_30), .c_2(out_31),
    .d_2(out_32));

  // Notes on the sheet:
  //   KEY STREAM GENERATOR
  //   Counter
endmodule

module Bit_Selector (
  input  BIT_SELECTOR,
  input  in_2,
  input  in_3,
  input  in_4,
  input  in_5,
  input  in_6,
  input  in_7,
  input  in_8,
  input  in_9,
  input  in_10,
  input  in_11,
  input  in_12,
  input  in_13,
  input  in_14,
  input  in_15,
  input  in_16,
  input  FLAG,
  input  LOCK,
  output out_19
);

  wire and_1_out, and_2_out, and_3_out, and_4_out, and_5_out, and_6_out, and_7_out, and_8_out, and_9_out,
       and_10_out, and_11_out, and_12_out, and_13_out, and_14_out, and_15_out, and_16_out, d_ff_1_q,
       d_ff_1_qn, d_ff_2_q, d_ff_2_qn, d_ff_3_q, d_ff_3_qn, d_ff_4_q, d_ff_4_qn, decoder_1_out_5,
       decoder_1_out_6, decoder_1_out_7, decoder_1_out_8, decoder_1_out_9, decoder_1_out_10,
       decoder_1_out_11, decoder_1_out_12, decoder_1_out_13, decoder_1_out_14, decoder_1_out_15,
       decoder_1_out_16, decoder_1_out_17, decoder_1_out_18, decoder_1_out_19, decoder_1_out_20;

  D_Flip_Flop d_ff_1 (.clk(FLAG), .D(d_ff_1_qn), .Q(d_ff_1_q), .Qn(d_ff_1_qn), .preset(LOCK));  // open: en, reset
  D_Flip_Flop d_ff_2 (.clk(d_ff_1_qn), .D(d_ff_2_qn), .Q(d_ff_2_q), .Qn(d_ff_2_qn), .preset(LOCK));  // open: en, reset
  D_Flip_Flop d_ff_3 (.clk(d_ff_2_qn), .D(d_ff_3_qn), .Q(d_ff_3_q), .Qn(d_ff_3_qn), .preset(LOCK));  // open: en, reset
  D_Flip_Flop d_ff_4 (.clk(d_ff_3_qn), .D(d_ff_4_qn), .Q(d_ff_4_q), .Qn(d_ff_4_qn), .preset(LOCK));  // open: en, reset
  Decoder decoder_1 (
    .MSB(d_ff_4_q), .in_2(d_ff_3_q), .in_3(d_ff_2_q), .LSB(d_ff_1_q), .out_5(decoder_1_out_5),
    .out_6(decoder_1_out_6), .out_7(decoder_1_out_7), .out_8(decoder_1_out_8), .out_9(decoder_1_out_9),
    .out_10(decoder_1_out_10), .out_11(decoder_1_out_11), .out_12(decoder_1_out_12),
    .out_13(decoder_1_out_13), .out_14(decoder_1_out_14), .out_15(decoder_1_out_15),
    .out_16(decoder_1_out_16), .out_17(decoder_1_out_17), .out_18(decoder_1_out_18),
    .out_19(decoder_1_out_19), .out_20(decoder_1_out_20));
  and and_1 (and_1_out, decoder_1_out_5, BIT_SELECTOR);
  and and_2 (and_2_out, decoder_1_out_6, in_2);
  and and_3 (and_3_out, decoder_1_out_7, in_3);
  and and_4 (and_4_out, decoder_1_out_9, in_5);
  and and_5 (and_5_out, decoder_1_out_8, in_4);
  and and_6 (and_6_out, decoder_1_out_11, in_7);
  and and_7 (and_7_out, decoder_1_out_10, in_6);
  and and_8 (and_8_out, decoder_1_out_13, in_9);
  and and_9 (and_9_out, decoder_1_out_12, in_8);
  or or_1 (out_19, and_1_out, and_2_out, and_3_out, and_5_out, and_4_out, and_7_out, and_6_out, and_9_out, and_8_out, and_11_out, and_10_out, and_13_out, and_12_out, and_14_out, and_15_out, and_16_out);
  and and_10 (and_10_out, decoder_1_out_15, in_11);
  and and_11 (and_11_out, decoder_1_out_14, in_10);
  and and_12 (and_12_out, decoder_1_out_17, in_13);
  and and_13 (and_13_out, decoder_1_out_16, in_12);
  and and_14 (and_14_out, decoder_1_out_18, in_14);
  and and_15 (and_15_out, decoder_1_out_19, in_15);
  and and_16 (and_16_out, decoder_1_out_20, in_16);
endmodule

// 2B-C
module _2_Bit_Counter (
  input  in_1,
  input  INIT_LSB,
  input  INIT_MSB,
  input  Lock,
  output LSB,
  output MSB
);

  wire And1_out, And2_out, And3_out, And4_out, d_ff_1_qn, d_ff_2_qn, not_1_out, not_2_out;

  and And1 (And1_out, INIT_LSB, Lock);
  D_Flip_Flop d_ff_1 (
    .clk(in_1), .D(d_ff_1_qn), .Q(LSB), .Qn(d_ff_1_qn), .preset(And1_out), .reset(And2_out));  // open: en
  and And2 (And2_out, not_1_out, Lock);
  not not_1 (not_1_out, INIT_LSB);
  D_Flip_Flop d_ff_2 (
    .clk(d_ff_1_qn), .D(d_ff_2_qn), .Q(MSB), .Qn(d_ff_2_qn), .preset(And3_out), .reset(And4_out));  // open: en
  and And3 (And3_out, INIT_MSB, Lock);
  and And4 (And4_out, not_2_out, Lock);
  not not_2 (not_2_out, INIT_MSB);

  // Notes on the sheet:
  //   COUNTER
endmodule

// QRG
module Quarter_Round_Generator (
  input  A,
  input  B,
  input  C,
  input  D,
  output a_2,
  output b_2,
  output c_2,
  output d_2
);

  wire adder_1_out, adder_3_out, Xor1_out, Xor2_out;

  Adder #(.width(1)) adder_1 (.a(B), .b(A), .out(adder_1_out));  // open: cin, cout
  xor Xor2 (Xor2_out, B, adder_3_out);
  xor Xor4 (b_2, Xor2_out, c_2);
  Adder #(.width(1)) adder_2 (.a(Xor2_out), .b(adder_1_out), .out(a_2));  // open: cin, cout
  xor Xor1 (Xor1_out, adder_1_out, D);
  xor Xor3 (d_2, a_2, Xor1_out);
  Adder #(.width(1)) adder_3 (.a(Xor1_out), .b(C), .out(adder_3_out));  // open: cin, cout
  Adder #(.width(1)) adder_4 (.a(adder_3_out), .b(d_2), .out(c_2));  // open: cin, cout

  // Notes on the sheet:
  //   Add1
  //   Add3
  //   QUARTER ROUND GENERATOR
  //   Add2
  //   Add4
endmodule

// PTI
module Plain_Text_Input (
  input  input_1,
  input  input_0,
  output flag,
  output Bit_Value
);

  or or_1 (flag, input_1, input_0);

  assign Bit_Value = input_1;

  // Notes on the sheet:
  //   PLAIN TEXT INPUT
endmodule

// DECODER
module Decoder (
  input  MSB,
  input  in_2,
  input  in_3,
  input  LSB,
  output out_5,
  output out_6,
  output out_7,
  output out_8,
  output out_9,
  output out_10,
  output out_11,
  output out_12,
  output out_13,
  output out_14,
  output out_15,
  output out_16,
  output out_17,
  output out_18,
  output out_19,
  output out_20
);

  wire not_1_out, not_2_out, not_3_out, not_4_out;

  not not_1 (not_1_out, MSB);
  not not_2 (not_2_out, in_2);
  not not_3 (not_3_out, in_3);
  not not_4 (not_4_out, LSB);
  and and_1 (out_5, not_1_out, not_2_out, not_3_out, not_4_out);
  and and_2 (out_6, not_1_out, not_2_out, not_3_out, LSB);
  and and_3 (out_7, not_1_out, not_2_out, in_3, not_4_out);
  and and_4 (out_8, not_1_out, not_2_out, in_3, LSB);
  and and_5 (out_9, not_1_out, in_2, not_3_out, not_4_out);
  and and_6 (out_10, not_1_out, in_2, not_3_out, LSB);
  and and_7 (out_11, not_1_out, in_2, in_3, not_4_out);
  and and_8 (out_12, not_1_out, in_2, in_3, LSB);
  and and_9 (out_13, MSB, not_2_out, not_3_out, not_4_out);
  and and_10 (out_14, MSB, not_2_out, not_3_out, LSB);
  and and_11 (out_15, MSB, not_2_out, in_3, not_4_out);
  and and_12 (out_16, MSB, not_2_out, in_3, LSB);
  and and_13 (out_17, MSB, in_2, not_3_out, not_4_out);
  and and_14 (out_18, MSB, in_2, not_3_out, LSB);
  and and_15 (out_19, MSB, in_2, in_3, not_4_out);
  and and_16 (out_20, MSB, in_2, in_3, LSB);

  // Notes on the sheet:
  //   DECODER
endmodule
